# Fritzing sketch draw (saved by Fritzing 0.9.2b)
breadboards: 1

parts:
  Raspberry_Pi2 = Raspberry Pi B rev1
  LED1 = RGB LED (com. cathode, rgb) [package="5 mm [THT]"]
  LED2 = LED - 5mm [color="Red (633nm)" package="5 mm [THT]"]
  J1 = Piezo Speaker
  R1 = Resistor [tolerance=±5% resistance=330 package=THT]
  R2 = Resistor [tolerance=±5% resistance=330 package=THT]
  R3 = Resistor [tolerance=±5% resistance=330 package=THT]

nets:
  N1: Raspberry_Pi2.GPIO_0, Raspberry_Pi2.5V
  N2: Raspberry_Pi2.GPIO_1, Raspberry_Pi2.GND, LED1.common_cathode, LED2.cathode, J1.pin1
  N3: Raspberry_Pi2.GPIO_23, J1.pin2
  N4: Raspberry_Pi2.GPIO_17, R1.Pin_0
  N5: Raspberry_Pi2.GPIO_18, LED2.anode
  N6: Raspberry_Pi2.GPIO_21, R2.Pin_0
  N7: Raspberry_Pi2.GPIO_22, R3.Pin_0
  N8: LED1.red_anode, R1.Pin_1
  N9: LED1.green_anode, R2.Pin_1
  N10: LED1.blue_anode, R3.Pin_1
